// Logisim project OiAK_Projekt.circ as structural Verilog: 14 circuits, main circuit main
module main (
  input  in_1,
  output [7:0] Accu,
  output [7:0] R0,
  output [7:0] R1,
  output [7:0] R2,
  output [7:0] R3,
  output [7:0] value,
  output [7:0] Bus_data
);

  wire A_e, A_s, alu_1_carry_out, alu_1_equal_flag, alu_1_zero, clk, clr, control_section_1_bus_1,
       control_section_1_iar_e, control_section_1_iar_s, control_section_1_ir_s, control_section_1_mar_s,
       control_section_1_r0_e, control_section_1_r0_s, control_section_1_r1_e, control_section_1_r1_s,
       control_section_1_r2_e, control_section_1_r2_s, control_section_1_r3_e, control_section_1_r3_s,
       control_section_1_ram_e, control_section_1_ram_s, control_section_1_tmp_s, cpu_clock_1_clk,
       cpu_clock_1_clk_e, cpu_clock_1_clk_s, flags_1_carry_in, flags_1_equal_out, flags_1_zero_out, flg_s,
       flg_str;
  wire [3:0] control_section_1_alu;
  wire [7:0] acc_1_output_data, alu_1_output_data, enable_8bit_1_outputdata, ir_1_output_data,
       tmp_1_output_data;

  ALU alu_1 (
    .output_data(alu_1_output_data), .A_input(acc_1_output_data), .equal_flag(alu_1_equal_flag),
    .B_input(tmp_1_output_data), .zero(alu_1_zero), .carry_in(flags_1_carry_in),
    .decoder_3bit_select(control_section_1_alu), .carry_out(alu_1_carry_out));
  Tmp tmp_1 (
    .Output_data(tmp_1_output_data),
    .Input_Data({Bus_data[0], Bus_data[1], Bus_data[2], Bus_data[3], Bus_data[4], Bus_data[5], Bus_data[6], Bus_data[7]}),
    .Set_value(control_section_1_tmp_s), .clock_in(clk));
  assign {Bus_data[0], Bus_data[1], Bus_data[2], Bus_data[3], Bus_data[4], Bus_data[5], Bus_data[6], Bus_data[7]} = A_e ? enable_8bit_1_outputdata : 8'bz;  // Controlled_Buffer controlled_buffer_1
  Enable_8bit enable_8bit_1 (.outputdata(enable_8bit_1_outputdata), .input_data(alu_1_output_data), .enable(A_e));
  ACC acc_1 (
    .Output_data(acc_1_output_data), .Acc(Accu),
    .Input_Data({Bus_data[0], Bus_data[1], Bus_data[2], Bus_data[3], Bus_data[4], Bus_data[5], Bus_data[6], Bus_data[7]}),
    .Set(A_s), .clk_in(clk));
  Flags flags_1 (
    .carry_out(alu_1_carry_out), .Equal(alu_1_equal_flag), .zero(alu_1_zero), .set_value(flg_s),
    .clk_in(clk), .store(flg_str), .clear_flags(clr), .carry_in(flags_1_carry_in),
    .Equal_out(flags_1_equal_out), .zero_out(flags_1_zero_out));
  Clock u_clk (.out(clk));
  Clock sysclk ();  // open: out
  Cpu_clock cpu_clock_1 (.clk_in(clk), .clk_e(cpu_clock_1_clk_e), .clk(cpu_clock_1_clk), .clk_s(cpu_clock_1_clk_s));
  registry registry_1 (
    .Output_data({Bus_data[0], Bus_data[1], Bus_data[2], Bus_data[3], Bus_data[4], Bus_data[5], Bus_data[6], Bus_data[7]}),
    .Value(R0), .Set(control_section_1_r0_s),
    .Input_Data({Bus_data[0], Bus_data[1], Bus_data[2], Bus_data[3], Bus_data[4], Bus_data[5], Bus_data[6], Bus_data[7]}),
    .Export_value(control_section_1_r0_e), .clock_in(clk));
  Control_Section control_section_1 (
    .clk_e(cpu_clock_1_clk_e), .MAR_S(control_section_1_mar_s), .Ram_E(control_section_1_ram_e),
    .R3_S(control_section_1_r3_s), .R2_E(control_section_1_r2_e), .RAM_S(control_section_1_ram_s),
    .clk_s(cpu_clock_1_clk_s), .TMP_S(control_section_1_tmp_s), .R1_S(control_section_1_r1_s),
    .R0_S(control_section_1_r0_s), .R1_E(control_section_1_r1_e), .clk(cpu_clock_1_clk),
    .R2_S(control_section_1_r2_s), .ACC_S(A_s), .ACC_E(A_e), .R3_E(control_section_1_r3_e),
    .R0_E(control_section_1_r0_e), .BUS_1(control_section_1_bus_1), .IAR_E(control_section_1_iar_e),
    .IR_S(control_section_1_ir_s), .IAR_S(control_section_1_iar_s), .IR_IN(ir_1_output_data),
    .carry_in(flags_1_carry_in), .zero_in(flags_1_zero_out), .Alu(control_section_1_alu), .flg_s(flg_s),
    .flg_str(flg_str), .Clear(clr), .equal(flags_1_equal_out));
  IAR iar_1 (
    .clear(in_1), .Set_data(control_section_1_iar_s), .clk_in(clk),
    .input_data({Bus_data[0], Bus_data[1], Bus_data[2], Bus_data[3], Bus_data[4], Bus_data[5], Bus_data[6], Bus_data[7]}),
    .Value(value), .in_6(control_section_1_iar_e),
    .Output_data({Bus_data[0], Bus_data[1], Bus_data[2], Bus_data[3], Bus_data[4], Bus_data[5], Bus_data[6], Bus_data[7]}),
    .bus_1(control_section_1_bus_1));
  registry registry_2 (
    .Output_data({Bus_data[0], Bus_data[1], Bus_data[2], Bus_data[3], Bus_data[4], Bus_data[5], Bus_data[6], Bus_data[7]}),
    .Value(R1), .Set(control_section_1_r1_s),
    .Input_Data({Bus_data[0], Bus_data[1], Bus_data[2], Bus_data[3], Bus_data[4], Bus_data[5], Bus_data[6], Bus_data[7]}),
    .Export_value(control_section_1_r1_e), .clock_in(clk));
  IR ir_1 (
    .Input_Data({Bus_data[0], Bus_data[1], Bus_data[2], Bus_data[3], Bus_data[4], Bus_data[5], Bus_data[6], Bus_data[7]}),
    .Set(control_section_1_ir_s), .clk_in(clk), .Output_Data(ir_1_output_data));
  // Probe on ir_1_output_data
  registry registry_3 (
    .Output_data({Bus_data[0], Bus_data[1], Bus_data[2], Bus_data[3], Bus_data[4], Bus_data[5], Bus_data[6], Bus_data[7]}),
    .Value(R2), .Set(control_section_1_r2_s),
    .Input_Data({Bus_data[0], Bus_data[1], Bus_data[2], Bus_data[3], Bus_data[4], Bus_data[5], Bus_data[6], Bus_data[7]}),
    .Export_value(control_section_1_r2_e), .clock_in(clk));
  registry registry_4 (
    .Output_data({Bus_data[0], Bus_data[1], Bus_data[2], Bus_data[3], Bus_data[4], Bus_data[5], Bus_data[6], Bus_data[7]}),
    .Value(R3), .Set(control_section_1_r3_s),
    .Input_Data({Bus_data[0], Bus_data[1], Bus_data[2], Bus_data[3], Bus_data[4], Bus_data[5], Bus_data[6], Bus_data[7]}),
    .Export_value(control_section_1_r3_e), .clock_in(clk));
  IRAM iram_1 (
    .Address({Bus_data[0], Bus_data[1], Bus_data[2], Bus_data[3], Bus_data[4], Bus_data[5], Bus_data[6], Bus_data[7]}),
    .Set_Addres(control_section_1_mar_s), .Set_Value(control_section_1_ram_s),
    .Export_Value(control_section_1_ram_e), .clk_in(clk),
    .Output_Data({Bus_data[0], Bus_data[1], Bus_data[2], Bus_data[3], Bus_data[4], Bus_data[5], Bus_data[6], Bus_data[7]}));
endmodule

module Enable_8bit (
  input  [7:0] input_data,
  input  enable,
  output [7:0] outputdata
);

  and and_1 (outputdata[0], input_data[0], enable);
  and and_2 (outputdata[1], input_data[1], enable);
  and and_3 (outputdata[2], input_data[2], enable);
  and and_4 (outputdata[3], input_data[3], enable);
  and and_5 (outputdata[4], input_data[4], enable);
  and and_6 (outputdata[5], input_data[5], enable);
  and and_7 (outputdata[6], input_data[6], enable);
  and and_8 (outputdata[7], input_data[7], enable);

  // Notes on the sheet:
  //   outputdata: pull=down
endmodule

module ALU (
  input  [7:0] A_input,
  input  [7:0] B_input,
  input  carry_in,
  input  [3:0] decoder_3bit_select,
  output equal_flag,
  output zero,
  output [7:0] output_data,
  output carry_out
);

  wire adder_1_cout, and_1_out, and_2_out, and_4_out, and_5_out, decoder_1_out3, decoder_1_out9, NOP,
       subtractor_1_bout;
  wire [7:0] adder_1_out, and_3_out, or_1_out, subtractor_1_out, xor_1_out;

  and and_1 (and_1_out, carry_in, decoder_1_out3);
  and and_2 (and_2_out, carry_in, decoder_1_out9);
  Subtractor subtractor_1 (.a(A_input), .b(B_input), .out(subtractor_1_out), .bin(and_2_out), .bout(subtractor_1_bout));
  Adder adder_1 (.a(A_input), .b(B_input), .out(adder_1_out), .cin(and_1_out), .cout(adder_1_cout));
  assign xor_1_out = A_input ^ B_input;  // XOR_Gate xor_1, 8 bits wide
  assign or_1_out = A_input | B_input;  // OR_Gate or_1, 8 bits wide
  assign and_3_out = A_input & B_input;  // AND_Gate and_3, 8 bits wide
  Decoder #(.select(4)) decoder_1 (
    .out0(NOP), .out3(decoder_1_out3), .out9(decoder_1_out9), .sel(decoder_3bit_select));  // open: out1, out2, out4, out5, out6, out7, out8, out10, out11, out12, out13, out14, out15, en
  Comparator comparator_1 (.a(A_input), .b(B_input), .eq(equal_flag));  // open: gt, lt
  and and_4 (and_4_out, subtractor_1_bout, decoder_1_out9);
  and and_5 (and_5_out, decoder_1_out3, adder_1_cout);
  or or_2 (carry_out, and_4_out, and_5_out);
  Multiplexer #(.select(4), .width(8), .enable("false")) multiplexer_1 (
    .in0({8{1'b0}}), .in1({8{1'b0}}), .in2({8{1'b0}}), .in3(adder_1_out), .in4(or_1_out), .in5(and_3_out),
    .in6(xor_1_out), .in7({8{1'b0}}), .in8({8{1'b0}}), .in9(subtractor_1_out), .in10({8{1'b0}}),
    .in11({8{1'b0}}), .in12({8{1'b0}}), .in13({8{1'b0}}), .in14({8{1'b0}}), .in15(A_input),
    .out(output_data), .sel(decoder_3bit_select));
  Comparator comparator_2 (.a(output_data), .b({8{1'b0}}), .eq(zero));  // open: gt, lt

  // Notes on the sheet:
  //   zero: pull=down
endmodule

module Stepper (
  input  reset,
  input  clk,
  output c1,
  output c2,
  output c3,
  output c4,
  output c5,
  output c6,
  output c7
);

  wire [2:0] counter_1_q;

  Counter #(.width(3), .max('h6), .ongoal("stay"), .trigger("falling")) counter_1 (
    .clr(reset), .up(1'b1), .clk(clk), .Q(counter_1_q));  // open: load, count, D, carry
  Decoder #(.select(3)) decoder_1 (
    .out0(c1), .out1(c2), .out2(c3), .out3(c4), .out4(c5), .out5(c6), .out6(c7), .sel(counter_1_q));  // open: out7, en
endmodule

module Control_Section (
  input  clk_s,
  input  clk,
  input  clk_e,
  input  carry_in,
  input  equal,
  input  zero_in,
  input  [7:0] IR_IN,
  output BUS_1,
  output MAR_S,
  output Ram_E,
  output ACC_S,
  output RAM_S,
  output ACC_E,
  output TMP_S,
  output Clear,
  output IAR_E,
  output R0_S,
  output R0_E,
  output R1_S,
  output R2_S,
  output R1_E,
  output R3_S,
  output R2_E,
  output IR_S,
  output IAR_S,
  output R3_E,
  output flg_str,
  output flg_s,
  output [3:0] Alu
);

  wire ADDC_A, ADDC_A_immed, ADDC_A_rr, and_3_out, and_4_out, and_13_out, and_15_out, and_16_out, and_17_out,
       and_18_out, and_19_out, and_20_out, and_21_out, and_22_out, and_23_out, and_24_out, and_25_out,
       and_26_out, and_27_out, and_28_out, and_29_out, and_30_out, and_31_out, and_32_out, and_33_out,
       and_34_out, and_35_out, and_36_out, and_37_out, and_38_out, and_39_out, and_41_out, and_44_out,
       and_45_out, and_46_out, and_47_out, and_48_out, and_50_out, and_51_out, and_53_out, and_54_out,
       and_55_out, and_56_out, and_57_out, and_58_out, and_59_out, and_60_out, and_61_out, and_62_out,
       and_63_out, and_64_out, ANL_A, CLR_PSW, decoder_1_out8, decoder_1_out11, decoder_1_out12,
       decoder_1_out14, decoder_2_out0, decoder_2_out1, decoder_2_out2, decoder_2_out3, immed, jmpA, Jump,
       mov_A_immed, mov_A_rr, mov_op_A, mov_op_data, mov_rr_A, mov_RR_immed, movA_op, NOP, or_1_out,
       or_2_out, or_4_out, or_5_out, or_6_out, or_7_out, or_8_out, or_15_out, or_16_out, or_17_out,
       or_18_out, or_20_out, or_21_out, or_22_out, or_23_out, or_24_out, ORL_A, ORL_A_immed, ORL_A_rr, R0,
       R1, R2, R3, stepper_1_c1, stepper_1_c2, stepper_1_c3, stepper_1_c4, stepper_1_c5, stepper_1_c6,
       stepper_1_c7, SUBB_A, XRL_A;

  or or_1 (or_1_out, ADDC_A_immed, mov_A_immed, ORL_A_immed, mov_RR_immed, Jump);
  Multiplexer #(.width(4), .enable("false")) multiplexer_1 (.in0(4'b0000), .in1(IR_IN[7:4]), .out(Alu), .sel(or_2_out));
  or or_2 (or_2_out, ORL_A, mov_rr_A, ANL_A, XRL_A, ADDC_A, SUBB_A);
  and and_1 (BUS_1, or_6_out, clk_e, clk, clk_s);
  or or_3 (IAR_E, and_3_out, and_4_out);
  and and_2 (flg_str, clk_s, clk_e, or_8_out, clk);
  or or_4 (or_4_out, ADDC_A, SUBB_A);
  or or_5 (or_5_out, ORL_A, XRL_A, ANL_A);
  or or_6 (or_6_out, stepper_1_c2, and_30_out, and_13_out);
  and and_3 (and_3_out, clk_e, stepper_1_c1);
  and and_4 (and_4_out, clk_e, stepper_1_c3, or_1_out);
  and and_5 (mov_A_rr, movA_op, IR_IN[3]);
  and and_6 (mov_rr_A, IR_IN[3], mov_op_A);
  and and_7 (mov_RR_immed, IR_IN[3], mov_op_data);
  and and_8 (mov_A_immed, mov_op_data, immed);
  and and_9 (ADDC_A_immed, immed, or_4_out);
  and and_10 (ADDC_A_rr, IR_IN[3], or_4_out);
  and and_11 (ORL_A_immed, immed, or_5_out);
  and and_12 (ORL_A_rr, IR_IN[3], or_5_out);
  and and_13 (and_13_out, stepper_1_c5, or_7_out);
  or or_7 (or_7_out, ORL_A_immed, mov_RR_immed, mov_A_immed);
  and and_14 (Clear, stepper_1_c3, CLR_PSW);
  or or_8 (or_8_out, and_15_out, and_16_out);
  or or_9 (Ram_E, and_17_out, and_18_out);
  or or_10 (ACC_E, and_19_out, and_20_out, and_21_out);
  or or_11 (R0_E, and_22_out, and_23_out);
  or or_12 (R1_E, and_24_out, and_25_out);
  or or_13 (R2_E, and_26_out, and_27_out);
  or or_14 (R3_E, and_28_out, and_29_out);
  and and_15 (and_15_out, stepper_1_c4, ADDC_A_immed);
  and and_16 (and_16_out, stepper_1_c3, ADDC_A_rr);
  and and_17 (and_17_out, clk_e, or_15_out, stepper_1_c4);
  and and_18 (and_18_out, clk_e, stepper_1_c2);
  and and_19 (and_19_out, clk_e, stepper_1_c4, or_18_out);
  and and_20 (and_20_out, clk_e, stepper_1_c3, mov_rr_A);
  and and_21 (and_21_out, stepper_1_c5, clk_e, or_16_out);
  and and_22 (and_22_out, or_17_out, R0, stepper_1_c3, clk_e);
  and and_23 (and_23_out, clk_e, 1'b0, R0, stepper_1_c4);
  and and_24 (and_24_out, or_17_out, R1, stepper_1_c3, clk_e);
  and and_25 (and_25_out, clk_e, R1, 1'b0, stepper_1_c4);
  and and_26 (and_26_out, or_17_out, R2, stepper_1_c3, clk_e);
  and and_27 (and_27_out, clk_e, R2, 1'b0, stepper_1_c4);
  and and_28 (and_28_out, or_17_out, R3, stepper_1_c3, clk_e);
  and and_29 (and_29_out, clk_e, R3, 1'b0, stepper_1_c4);
  or or_15 (or_15_out, Jump, ORL_A_immed, mov_RR_immed, mov_A_immed, ADDC_A_immed);
  or or_16 (or_16_out, ADDC_A_immed, ORL_A_immed);
  or or_17 (or_17_out, jmpA, ADDC_A_rr, ORL_A_rr, mov_A_rr);
  and and_30 (and_30_out, ADDC_A_immed, stepper_1_c6);
  or or_18 (or_18_out, ORL_A_rr, ADDC_A_rr);
  or or_19 (Jump, and_32_out, and_31_out, and_36_out, and_35_out, and_41_out, and_39_out);
  and and_31 (and_31_out, and_34_out, decoder_2_out0);
  and and_32 (and_32_out, and_33_out, decoder_2_out0);
  and and_33 (and_33_out, ~carry_in, ANL_A);  // AND_Gate
  and and_34 (and_34_out, carry_in, ORL_A);
  and and_35 (and_35_out, and_38_out, decoder_2_out0);
  and and_36 (and_36_out, and_37_out, decoder_2_out0);
  and and_37 (and_37_out, ~zero_in, mov_op_data);  // AND_Gate
  and and_38 (and_38_out, zero_in, XRL_A);
  and and_39 (and_39_out, ~equal, decoder_1_out11);  // AND_Gate
  and and_40 (CLR_PSW, decoder_1_out12, decoder_2_out3);
  and and_41 (and_41_out, decoder_1_out8, immed);
  Decoder #(.select(4)) decoder_1 (
    .out0(NOP), .out3(ADDC_A), .out4(ORL_A), .out5(ANL_A), .out6(XRL_A), .out7(mov_op_data),
    .out8(decoder_1_out8), .out9(SUBB_A), .out11(decoder_1_out11), .out12(decoder_1_out12),
    .out14(decoder_1_out14), .out15(mov_op_A), .sel(IR_IN[7:4]));  // open: out1, out2, out10, out13, en
  and and_42 (jmpA, decoder_1_out8, IR_IN[3]);
  Decoder #(.select(4)) decoder_2 (
    .out0(decoder_2_out0), .out1(decoder_2_out1), .out2(decoder_2_out2), .out3(decoder_2_out3), .out4(immed),
    .sel(IR_IN[3:0]));  // open: out5, out6, out7, out8, out9, out10, out11, out12, out13, out14, out15, en
  and and_43 (movA_op, decoder_1_out14, ~decoder_2_out0, ~decoder_2_out1, ~decoder_2_out2, ~decoder_2_out3);  // AND_Gate
  Stepper stepper_1 (
    .c4(stepper_1_c4), .c5(stepper_1_c5), .c3(stepper_1_c3), .c7(stepper_1_c7), .c2(stepper_1_c2),
    .c6(stepper_1_c6), .c1(stepper_1_c1), .reset(stepper_1_c7), .clk(clk));
  or or_20 (or_20_out, mov_A_immed, ORL_A_rr, ADDC_A_rr);
  or or_21 (or_21_out, ADDC_A_rr, ORL_A_rr);
  or or_22 (or_22_out, mov_A_immed, mov_RR_immed, ORL_A_immed, Jump, ADDC_A_immed);
  or or_23 (or_23_out, ADDC_A_immed, ORL_A_immed);
  or or_24 (or_24_out, ADDC_A_immed, ORL_A_immed);
  and and_44 (and_44_out, clk_s, stepper_1_c3, or_22_out);
  and and_45 (and_45_out, clk_s, stepper_1_c1);
  and and_46 (and_46_out, or_23_out, clk_s, stepper_1_c5);
  and and_47 (and_47_out, clk_s, stepper_1_c4, or_20_out);
  and and_48 (and_48_out, clk_s, stepper_1_c3, mov_A_rr);
  and and_49 (RAM_S, clk_s, 1'b0);
  and and_50 (and_50_out, clk_s, stepper_1_c3, or_21_out);
  and and_51 (and_51_out, clk_s, stepper_1_c4, or_24_out);
  and and_52 (IR_S, clk_s, stepper_1_c2);
  and and_53 (and_53_out, clk_s, stepper_1_c4, Jump);
  and and_54 (and_54_out, clk_s, stepper_1_c3, jmpA);
  and and_55 (and_55_out, mov_RR_immed, clk_s, stepper_1_c4, R0);
  and and_56 (and_56_out, mov_rr_A, clk_s, stepper_1_c3, R0);
  and and_57 (and_57_out, mov_RR_immed, clk_s, stepper_1_c4, R1);
  and and_58 (and_58_out, mov_rr_A, clk_s, stepper_1_c3, R1);
  and and_59 (and_59_out, mov_RR_immed, clk_s, stepper_1_c4, R2);
  and and_60 (and_60_out, mov_rr_A, clk_s, stepper_1_c3, R2);
  and and_61 (and_61_out, mov_RR_immed, clk_s, stepper_1_c4, R3);
  and and_62 (and_62_out, mov_rr_A, clk_s, stepper_1_c3, R3);
  or or_25 (IAR_S, and_53_out, and_54_out);
  and and_63 (and_63_out, clk_s, stepper_1_c5, ADDC_A_rr);
  and and_64 (and_64_out, clk_s, stepper_1_c6, ADDC_A_immed);
  or or_26 (MAR_S, and_44_out, and_45_out);
  or or_27 (ACC_S, and_46_out, and_47_out, and_48_out);
  or or_28 (TMP_S, and_50_out, and_51_out);
  or or_29 (R0_S, and_55_out, and_56_out);
  or or_30 (R1_S, and_57_out, and_58_out);
  or or_31 (R2_S, and_59_out, and_60_out);
  or or_32 (R3_S, and_61_out, and_62_out);
  or or_33 (flg_s, and_63_out, and_64_out);
  Decoder #(.select(2)) decoder_3 (.out0(R0), .out1(R1), .out2(R2), .out3(R3), .sel(IR_IN[1:0]), .en(IR_IN[3]));

  // Other names for the same wires on the sheet: fck = clk; fcs = clk_s; RR = IR_IN[3]

  // Notes on the sheet:
  //   BUS_1: pull=down
  //   IAR_E: pull=down
endmodule

module registry (
  input  [7:0] Input_Data,
  input  Set,
  input  clock_in,
  input  Export_value,
  output [7:0] Value,
  output [7:0] Output_data
);

  wire [7:0] enable_8bit_1_outputdata;

  Register #(.trigger("falling")) register_1 (.D(Input_Data), .en(Set), .clk(clock_in), .Q(Value));  // open: clr
  Enable_8bit enable_8bit_1 (.outputdata(enable_8bit_1_outputdata), .input_data(Value), .enable(Export_value));
  assign Output_data = Export_value ? enable_8bit_1_outputdata : 8'bz;  // Controlled_Buffer controlled_buffer_1

  // Notes on the sheet:
  //   Output_data: pull=down
  //   Input_Data: pull=down
  //   Value: pull=down
endmodule

module Tmp (
  input  [7:0] Input_Data,
  input  clock_in,
  input  Set_value,
  output [7:0] Output_data
);

  wire [7:0] controlled_buffer_1_out;

  assign controlled_buffer_1_out = Set_value ? Input_Data : 8'bz;  // Controlled_Buffer controlled_buffer_1
  Register #(.trigger("falling")) register_1 (
    .D(controlled_buffer_1_out), .en(Set_value), .clk(clock_in), .Q(Output_data));  // open: clr

  // Notes on the sheet:
  //   Input_Data: pull=down
endmodule

module Bus_1 (
  input  clear,
  input  load_value,
  input  set,
  input  [7:0] in_4,
  output [7:0] Output_data
);

  Counter #(.ongoal("stay")) counter_1 (
    .clr(clear), .load(load_value), .clk(set), .D(in_4), .Q(Output_data));  // open: up, count, carry
endmodule

module ACC (
  input  [7:0] Input_Data,
  input  Set,
  input  clk_in,
  output [7:0] Acc,
  output [7:0] Output_data
);

  Register #(.trigger("falling")) register_1 (.D(Input_Data), .en(Set), .clk(clk_in), .Q(Acc));  // open: clr

  assign Output_data = Acc;
endmodule

module Cpu_clock (
  input  clk_in,
  output clk,
  output clk_s,
  output clk_e
);

  wire and_1_out, j_k_ff_1_qn;

  J_K_Flip_Flop j_k_ff_1 (.J(1'b1), .K(1'b1), .clk(clk_in), .Q(clk), .Qn(j_k_ff_1_qn));  // open: preset, reset
  and and_1 (and_1_out, j_k_ff_1_qn, clk_in);
  not not_1 (clk_e, and_1_out);

  assign clk_s = clk;
endmodule

module IAR (
  input  clear,
  input  Set_data,
  input  bus_1,
  input  clk_in,
  input  [7:0] input_data,
  input  in_6,
  output [7:0] Value,
  output [7:0] Output_data
);

  wire [7:0] enable_8bit_1_outputdata;

  Counter #(.ongoal("stay"), .trigger("falling")) counter_1 (
    .clr(clear), .load(Set_data), .count(bus_1), .clk(clk_in), .D(input_data), .Q(Value));  // open: up, carry
  Enable_8bit enable_8bit_1 (.outputdata(enable_8bit_1_outputdata), .input_data(Value), .enable(in_6));
  assign Output_data = in_6 ? enable_8bit_1_outputdata : 8'bz;  // Controlled_Buffer controlled_buffer_1
endmodule

module IR (
  input  [7:0] Input_Data,
  input  Set,
  input  clk_in,
  output [7:0] Output_Data
);

  Register #(.trigger("falling")) register_1 (.D(Input_Data), .en(Set), .clk(clk_in), .Q(Output_Data));  // open: clr

  // Notes on the sheet:
  //   Input_Data: pull=down
endmodule

module IRAM (
  input  [7:0] Address,
  input  Set_Addres,
  input  Set_Value,
  input  Export_Value,
  input  clk_in,
  output [7:0] Output_Data
);

  wire [7:0] controlled_buffer_1_out, enable_8bit_1_outputdata, ram_1_dout, undriven;

  assign controlled_buffer_1_out = Set_Addres ? Address : 8'bz;  // Controlled_Buffer controlled_buffer_1
  RAM #(.trigger("falling"), .databus("bibus")) ram_1 (
    .addr(controlled_buffer_1_out), .we(Set_Value), .oe(Export_Value), .clk(clk_in), .din(undriven),
    .dout(ram_1_dout));
  assign Output_Data = Export_Value ? enable_8bit_1_outputdata : 8'bz;  // Controlled_Buffer controlled_buffer_2
  Enable_8bit enable_8bit_1 (.outputdata(enable_8bit_1_outputdata), .input_data(ram_1_dout), .enable(Export_Value));
endmodule

module Flags (
  input  carry_out,
  input  Equal,
  input  zero,
  input  set_value,
  input  clk_in,
  input  store,
  input  clear_flags,
  output carry_in,
  output Equal_out,
  output zero_out
);

  wire not_1_out, not_2_out, not_3_out, register_1_q, register_2_q, register_3_q;

  Register #(.width(1), .trigger("low")) register_1 (
    .D(carry_out), .en(store), .clk(not_1_out), .Q(register_1_q));  // open: clr
  not not_1 (not_1_out, clk_in);
  not not_2 (not_2_out, clk_in);
  not not_3 (not_3_out, clk_in);
  Register #(.width(1), .trigger("low")) register_2 (
    .D(Equal), .en(store), .clk(not_2_out), .Q(register_2_q));  // open: clr
  Register #(.width(1), .trigger("low")) register_3 (
    .D(zero), .en(store), .clk(not_3_out), .Q(register_3_q));  // open: clr
  Register #(.width(1), .trigger("falling")) register_4 (
    .D(register_1_q), .en(set_value), .clk(clk_in), .Q(carry_in), .clr(clear_flags));
  Register #(.width(1), .trigger("falling")) register_5 (
    .D(register_2_q), .en(set_value), .clk(clk_in), .Q(Equal_out), .clr(clear_flags));
  Register #(.width(1), .trigger("falling")) register_6 (
    .D(register_3_q), .en(set_value), .clk(clk_in), .Q(zero_out), .clr(clear_flags));

  // Notes on the sheet:
  //   zero: pull=down
endmodule
